# Fritzing sketch Schema (saved by Fritzing 0.9.3b)

parts:
  Raspberry_Pi = Raspberry Pi 3 [part_number=RPI-3-V1.2]
  Part1 = KY-015 Temperature & Humidity Sensor Module [package="Breakout board"]

nets:
  N1: Raspberry_Pi.GIPO4, Part1.Vin
  N2: Raspberry_Pi.GND, Part1.-
  N3: Raspberry_Pi.5V, Part1.S

custom parts:
  KY-015 Temperature & Humidity Sensor Module: KY-015 temperature and humidity sensor module, provides a low-latency serial interface to measure humidity and temperature.
